# Fritzing sketch Basic (saved by Fritzing 0.9.3b)
breadboards: 1

parts:
  RE1 = Rotary Encoder [package=THT]
  D1 = Rectifier Diode [part_number=1N4001 package="300 mil [THT]"]
  D2 = Rectifier Diode [part_number=1N4001 package="300 mil [THT]"]
  RE2 = Rotary Encoder [package=THT]
  D3 = Rectifier Diode [part_number=1N4001 package="300 mil [THT]"]
  D4 = Rectifier Diode [part_number=1N4001 package="300 mil [THT]"]
  RE3 = Rotary Encoder [package=THT]
  D5 = Rectifier Diode [part_number=1N4001 package="300 mil [THT]"]
  D6 = Rectifier Diode [part_number=1N4001 package="300 mil [THT]"]
  Part1 = Arduino Nano (Rev3.0)
  D7 = Rectifier Diode [part_number=1N4001 package="300 mil [THT]"]
  D8 = Rectifier Diode [part_number=1N4001 package="300 mil [THT]"]
  D9 = Rectifier Diode [part_number=1N4001 package="300 mil [THT]"]

nets:
  N1: RE1.EncoderPinA, D1.cathode
  N2: RE1.EncoderPinC, Part1.D6
  N3: RE1.EncoderPinB, D2.cathode
  N4: D1.anode, D4.anode, D6.anode, Part1.D5
  N5: D2.anode, D3.anode, D5.anode, Part1.D4
  N6: RE2.EncoderPinA, D4.cathode
  N7: RE2.EncoderPinC, Part1.D7
  N8: RE2.EncoderPinB, D3.cathode
  N9: RE3.EncoderPinA, D6.cathode
  N10: RE3.EncoderPinC, Part1.D8
  N11: RE3.EncoderPinB, D5.cathode
  N12: Part1.D3, D7.anode, D8.anode, D9.anode
