# Fritzing sketch Waypoint (saved by Fritzing 0.9.3b)
breadboards: 1

parts:
  Part1 = Arduino Mega ADK (Rev3)
  U1 = LCD-16X2 [package=lcd-16x2_noholes]
  R1 = Rotary Potentiometer (Small) [maximum_resistance=100kΩ package=THT]
  R2 = Resistor [tolerance=±5% resistance=220 package=THT]
  D1 = Diode [package=diode-1n4148]
  D2 = Diode [package=diode-1n4148]
  D3 = Diode [package=diode-1n4148]
  D4 = Diode [package=diode-1n4148]
  D5 = Diode [package=diode-1n4148]
  RE1 = Rotary Encoder [package=THT]
  RE2 = Rotary Encoder [package=THT]
  S1 = Pushbutton [package="[THT]"]

nets:
  N1: Part1.D12_PWM, U1.RS
  N2: Part1.D11_PWM, U1.E
  5V: Part1.5V, U1.VDD, R1.leg1, R2.Pin_0, RE1.EncoderPinC, RE2.EncoderPinC, S1.Pin_3, S1.Pin_4
  GND: Part1.GND, U1.VSS, U1.R_W, U1.K, R1.leg2
  N3: Part1.D2_PWM, U1.DB7
  N4: Part1.D3_PWM, U1.DB6
  N5: Part1.D4_PWM, U1.DB5
  N6: Part1.D5_PWM, U1.DB4
  N7: Part1.D34, D1.A, D4.A
  N8: Part1.D35, D2.A, D5.A
  N9: Part1.D36, D3.A
  N10: U1.VO, R1.wiper
  N11: U1.A, R2.Pin_1
  N12: S1.Pin_1, S1.Pin_2
